# Fritzing sketch EPROM_Reader Schematic (saved by Fritzing 0.9.3b)
breadboards: 1

parts:
  Part1 = Arduino Mega 2560 (Rev3)
  IC1 = IC, DIP package, 24 pins [chip_label=D2732A]

nets:
  N1: Part1.5V, IC1.pin24
  N2: Part1.D22, IC1.pin8
  N3: Part1.D23, IC1.pin7
  N4: Part1.D24, IC1.pin6
  N5: Part1.D25, IC1.pin5
  N6: Part1.D26, IC1.pin4
  N7: Part1.D27, IC1.pin3
  N8: Part1.D28, IC1.pin1
  N9: Part1.D29, IC1.pin2
  N10: Part1.D34, IC1.pin21
  N11: Part1.D35, IC1.pin19
  N12: Part1.D36, IC1.pin22
  N13: Part1.D37, IC1.pin23
  N14: Part1.D42, IC1.pin17
  N15: Part1.D43, IC1.pin16
  N16: Part1.D44, IC1.pin15
  N17: Part1.D45, IC1.pin14
  N18: Part1.D46, IC1.pin13
  N19: Part1.D47, IC1.pin11
  N20: Part1.D48, IC1.pin10
  N21: Part1.D49, IC1.pin9
  N22: Part1.GND, IC1.pin12, IC1.pin18, IC1.pin20

notes:
  Yellow = Data Bus
  Blue = Address Bus
  Red = +5V
  Black = GND
